# Fritzing sketch LSM_FDM_EDISON (saved by Fritzing 0.9.0b)
breadboards: 1

parts:
  R2 = Resistor [tolerance=±5% resistance=1k package=THT]
  R1 = Resistor [tolerance=±5% resistance=1k package=THT]
  Q1 = LTR-301 [package=ltr-301]
  LED1 = LED - 5mm [color="Green (570nm)" package="5 mm [THT]"]
  Q4 = NPN-Transistor [part_number="S8050 (EBC)" package="TO92 [THT]"]
  Q2 = NPN-Transistor [part_number="S8050 (EBC)" package="TO92 [THT]"]
  R3 = Resistor [tolerance=±5% resistance=1k package=THT]
  R4 = Resistor [tolerance=±5% resistance=1k package=THT]
  R5 = Resistor [tolerance=±5% resistance=100k package=THT]
  J1 = screw terminal, 3 pins [part_number="C E(Outdoors) E(Indoors)"]
  Q3 = NPN-Transistor [part_number="S8050 (EBC)" package="TO92 [THT]"]
  R6 = Resistor [tolerance=±5% resistance=100k package=THT]
  J3 = screw terminal, 3 pins [part_number="C E(Outdoors) E(Indoors)"]
  LED2 = LED - 5mm [color="Green (570nm)" package="5 mm [THT]"]
  Q5 = NPN-Transistor [part_number="S8050 (EBC)" package="TO92 [THT]"]
  Q6 = NPN-Transistor [part_number="S8050 (EBC)" package="TO92 [THT]"]
  Q7 = NPN-Transistor [part_number="S8050 (EBC)" package="TO92 [THT]"]
  R7 = Resistor [tolerance=±5% resistance=1k package=THT]
  R8 = Resistor [tolerance=±5% resistance=1k package=THT]
  R9 = Resistor [tolerance=±5% resistance=1k package=THT]
  R10 = Resistor [tolerance=±5% resistance=1k package=THT]
  Q8 = LTR-301 [package=ltr-301]
  R11 = Resistor [tolerance=±5% resistance=100k package=THT]
  R12 = Resistor [tolerance=±5% resistance=100k package=THT]
  J4 = screw terminal, 3 pins [part_number="C E(Outdoors) E(Indoors)"]
  J5 = screw terminal, 3 pins [part_number="C E(Outdoors) E(Indoors)"]
  LED3 = LED - 5mm [color="Green (570nm)" package="5 mm [THT]"]
  LED4 = LED - 5mm [color="Green (570nm)" package="5 mm [THT]"]
  Q9 = NPN-Transistor [part_number="S8050 (EBC)" package="TO92 [THT]"]
  Q10 = NPN-Transistor [part_number="S8050 (EBC)" package="TO92 [THT]"]
  Q11 = NPN-Transistor [part_number="S8050 (EBC)" package="TO92 [THT]"]
  Q12 = NPN-Transistor [part_number="S8050 (EBC)" package="TO92 [THT]"]
  Q13 = NPN-Transistor [part_number="S8050 (EBC)" package="TO92 [THT]"]
  Q14 = NPN-Transistor [part_number="S8050 (EBC)" package="TO92 [THT]"]
  R13 = Resistor [tolerance=±5% resistance=1k package=THT]
  R14 = Resistor [tolerance=±5% resistance=1k package=THT]
  R15 = Resistor [tolerance=±5% resistance=1k package=THT]
  R16 = Resistor [tolerance=±5% resistance=1k package=THT]
  R17 = Resistor [tolerance=±5% resistance=1k package=THT]
  R18 = Resistor [tolerance=±5% resistance=1k package=THT]
  R19 = Resistor [tolerance=±5% resistance=1k package=THT]
  R20 = Resistor [tolerance=±5% resistance=1k package=THT]
  Q15 = LTR-301 [package=ltr-301]
  Q16 = LTR-301 [package=ltr-301]
  J2 = screw terminal, 6 pins

nets:
  N1: R2.Pin_0, Q2.C
  N2: R2.Pin_1, R1.Pin_1, R3.Pin_1, R4.Pin_1, R7.Pin_1, R8.Pin_1, R9.Pin_1, R10.Pin_1, R13.Pin_1, R14.Pin_1, R15.Pin_1, R16.Pin_1, R17.Pin_1, R18.Pin_1, R19.Pin_1, R20.Pin_1, J2.pin1
  N3: R1.Pin_0, Q1.C, J1.pin1
  N4: Q1.E, Q2.B, R5.Pin_0, J1.pin2
  N5: LED1.cathode, Q4.C
  N6: LED1.anode, R4.Pin_0
  GND: Q4.E, R5.Pin_1, Q3.E, R6.Pin_1, Q5.E, Q7.E, R11.Pin_1, R12.Pin_1, Q9.E, Q10.E, Q13.E, Q14.E, J2.pin6
  N7: Q4.B, Q2.E, J1.pin3, Q3.B
  N8: R3.Pin_0, Q3.C, J2.pin2
  N9: R6.Pin_0, J3.pin2, Q6.B, Q8.E
  N10: J3.pin1, R7.Pin_0, Q8.C
  N11: J3.pin3, Q5.B, Q6.E, Q7.B
  N12: LED2.cathode, Q5.C
  N13: LED2.anode, R8.Pin_0
  N14: Q6.C, R10.Pin_0
  N15: Q7.C, R9.Pin_0, J2.pin3
  N16: R11.Pin_0, J5.pin2, Q11.B, Q15.E
  N17: R12.Pin_0, J4.pin2, Q12.B, Q16.E
  N18: J4.pin1, R14.Pin_0, Q16.C
  N19: J4.pin3, Q10.B, Q12.E, Q14.B
  N20: J5.pin1, R13.Pin_0, Q15.C
  N21: J5.pin3, Q9.B, Q11.E, Q13.B
  N22: LED3.cathode, Q9.C
  N23: LED3.anode, R15.Pin_0
  N24: LED4.cathode, Q10.C
  N25: LED4.anode, R16.Pin_0
  N26: Q11.C, R19.Pin_0
  N27: Q12.C, R20.Pin_0
  N28: Q13.C, R17.Pin_0, J2.pin4
  N29: Q14.C, R18.Pin_0, J2.pin5
