# Fritzing sketch LSM_FDM_EDISON_old (saved by Fritzing 0.8.7b)
breadboards: 1

parts:
  U1 = Voltage Regulator - 5V [package="DPak [SMD]"]
  R2 = Resistor [tolerance=±5% resistance=220 package=THT]
  R1 = Resistor [tolerance=±5% resistance=1k package=THT]
  Q1 = LTR-301 [package=ltr-301]
  LED1 = LED - 5mm [color="Green (570nm)" package="5 mm [THT]"]
  Q4 = NPN-Transistor [part_number="S8050 (EBC)" package="TO92 [THT]"]
  Part2 = Arduino Uno (Rev3)
  Q3 = NPN-Transistor [part_number="BC547 (CBE)" package="TO92 [THT]"]
  Q2 = NPN-Transistor [part_number="S8050 (EBC)" package="TO92 [THT]"]
  R3 = Resistor [tolerance=±5% resistance=1k package=THT]
  R4 = Resistor [tolerance=±5% resistance=1k package=THT]
  S1 = SPST Switch [package=switche-dpdt]
  LED2 = LED - 5mm [color="Green (570nm)" package="5 mm [THT]"]
  Q5 = NPN-Transistor [part_number="S8050 (EBC)" package="TO92 [THT]"]
  Q6 = NPN-Transistor [part_number="S8050 (EBC)" package="TO92 [THT]"]
  Q7 = NPN-Transistor [part_number="BC547 (CBE)" package="TO92 [THT]"]
  R5 = Resistor [tolerance=±5% resistance=1k package=THT]
  R6 = Resistor [tolerance=±5% resistance=220 package=THT]
  R7 = Resistor [tolerance=±5% resistance=1k package=THT]
  R8 = Resistor [tolerance=±5% resistance=1k package=THT]
  Q8 = LTR-301 [package=ltr-301]
  S2 = SPST Switch [package=switche-dpdt]
  LED3 = LED - 5mm [color="Green (570nm)" package="5 mm [THT]"]
  Q9 = NPN-Transistor [part_number="S8050 (EBC)" package="TO92 [THT]"]
  Q10 = NPN-Transistor [part_number="BC547 (CBE)" package="TO92 [THT]"]
  Q11 = NPN-Transistor [part_number="S8050 (EBC)" package="TO92 [THT]"]
  R9 = Resistor [tolerance=±5% resistance=1k package=THT]
  R10 = Resistor [tolerance=±5% resistance=1k package=THT]
  R11 = Resistor [tolerance=±5% resistance=220 package=THT]
  R12 = Resistor [tolerance=±5% resistance=1k package=THT]
  Q12 = LTR-301 [package=ltr-301]
  S3 = SPST Switch [package=switche-dpdt]
  LED4 = LED - 5mm [color="Green (570nm)" package="5 mm [THT]"]
  Q13 = NPN-Transistor [part_number="S8050 (EBC)" package="TO92 [THT]"]
  Q14 = NPN-Transistor [part_number="S8050 (EBC)" package="TO92 [THT]"]
  Q15 = NPN-Transistor [part_number="BC547 (CBE)" package="TO92 [THT]"]
  R13 = Resistor [tolerance=±5% resistance=1k package=THT]
  R14 = Resistor [tolerance=±5% resistance=1k package=THT]
  R15 = Resistor [tolerance=±5% resistance=220 package=THT]
  R16 = Resistor [tolerance=±5% resistance=1k package=THT]
  Q16 = LTR-301 [package=ltr-301]
  S4 = SPST Switch [package=switche-dpdt]
  LED5 = LED - 5mm [color="Red (633nm)" package="5 mm [THT]"]
  R17 = Resistor [tolerance=±5% resistance=220 package=THT]
  LED6 = LED - 5mm [color="Green (570nm)" package="5 mm [THT]"]
  R18 = Resistor [tolerance=±5% resistance=220 package=THT]
  LED7 = LED - 5mm [color="Red (633nm)" package="5 mm [THT]"]
  LED8 = LED - 5mm [color="Green (570nm)" package="5 mm [THT]"]
  R19 = Resistor [tolerance=±5% resistance=220 package=THT]
  R20 = Resistor [tolerance=±5% resistance=220 package=THT]
  LED9 = LED - 5mm [color="Red (633nm)" package="5 mm [THT]"]
  LED10 = LED - 5mm [color="Green (570nm)" package="5 mm [THT]"]
  R21 = Resistor [tolerance=±5% resistance=220 package=THT]
  R22 = Resistor [tolerance=±5% resistance=220 package=THT]
  LED11 = LED - 5mm [color="Red (633nm)" package="5 mm [THT]"]
  LED12 = LED - 5mm [color="Green (570nm)" package="5 mm [THT]"]
  R23 = Resistor [tolerance=±5% resistance=220 package=THT]
  R24 = Resistor [tolerance=±5% resistance=220 package=THT]
  SG1 = Buzzer 12mm [package=buzzer-cmt1603]
  LED13 = LED - 5mm [color="Red (633nm)" package="5 mm [THT]"]
  R25 = Resistor [tolerance=±5% resistance=220 package=THT]
  U2 = RELAY [package=relay-t9a-2]
  U3 = RELAY [package=relay-t9a-2]
  U4 = RELAY [package=relay-t9a-2]
  J1 = Screw terminal - 2 pins [package=THT]
  J2 = Screw terminal - 2 pins [package=THT]
  J3 = Screw terminal - 2 pins [package=THT]
  HC-SR04 = IC, DIP package, 4 pins [chip_label=IC]
  Part3 = XBee Explorer Regulated

nets:
  9V: U1.input_voltage
  GND: U1.GND, Q4.E, Part2.GND, Q3.E, Q5.E, Q7.E, Q9.E, Q10.E, Q13.E, Q15.E, R17.Pin_1, R18.Pin_1, R19.Pin_1, R20.Pin_1, R21.Pin_1, R22.Pin_1, R23.Pin_1, R24.Pin_1, SG1.2, R25.Pin_1, U2.COIL2, U3.COIL2, U4.COIL2, HC-SR04.pin4, Part3.GND
  5V: U1.output_voltage, R2.Pin_1, R1.Pin_1, Part2.VIN, R3.Pin_1, R4.Pin_1, R5.Pin_1, R6.Pin_1, R7.Pin_1, R8.Pin_1, R9.Pin_1, R10.Pin_1, R11.Pin_1, R12.Pin_1, R13.Pin_1, R14.Pin_1, R15.Pin_1, R16.Pin_1, HC-SR04.pin1, Part3.5V
  N1: R2.Pin_0, Q2.C
  N2: R1.Pin_0, Q1.C
  N3: Q1.E, S1.P
  N4: LED1.cathode, Q4.C
  N5: LED1.anode, R4.Pin_0
  N6: Q4.B, Q3.B, Q2.E, S1.O
  N7: Part2.A0, SG1.1, U4.COIL1
  N8: Part2.A1, LED13.anode, U3.COIL1
  N9: Part2.A2, U2.COIL1
  N10: Part2.A3, Part3.DIO12
  N11: Part2.D8, Q10.C, R12.Pin_0
  N12: Part2.D9_PWM, LED9.anode, Part3.DIO4
  N13: Part2.D10_PWM/SS, LED10.anode, Part3.DIO5
  N14: Part2.D11_PWM/MOSI, Q15.C, R16.Pin_0
  N15: Part2.D12/MISO, LED11.anode, Part3.DIO9
  N16: Part2.D13/SCK, LED12.anode, Part3.DIO11
  N17: Part2.D0/RX, HC-SR04.pin3
  N18: Part2.D1/TX, HC-SR04.pin2
  N19: Part2.D2, Q3.C, R3.Pin_0
  N20: Part2.D3_PWM, LED5.anode, Part3.DIO0
  N21: Part2.D4, LED6.anode, Part3.DIO1
  N22: Part2.D5_PWM, Q7.C, R8.Pin_0
  N23: Part2.D6_PWM, LED7.anode, Part3.DIO2
  N24: Part2.D7, LED8.anode, Part3.DIO3
  N25: Q2.B, S1.S
  N26: LED2.cathode, Q5.C
  N27: LED2.anode, R7.Pin_0
  N28: Q5.B, Q6.E, Q7.B, S2.O
  N29: Q6.B, S2.S
  N30: Q6.C, R6.Pin_0
  N31: R5.Pin_0, Q8.C
  N32: Q8.E, S2.P
  N33: LED3.cathode, Q9.C
  N34: LED3.anode, R10.Pin_0
  N35: Q9.B, Q10.B, Q11.E, S3.O
  N36: Q11.B, S3.S
  N37: Q11.C, R11.Pin_0
  N38: R9.Pin_0, Q12.C
  N39: Q12.E, S3.P
  N40: LED4.cathode, Q13.C
  N41: LED4.anode, R14.Pin_0
  N42: Q13.B, Q14.E, Q15.B, S4.O
  N43: Q14.B, S4.S
  N44: Q14.C, R15.Pin_0
  N45: R13.Pin_0, Q16.C
  N46: Q16.E, S4.P
  N47: LED5.cathode, R17.Pin_0
  N48: LED6.cathode, R18.Pin_0
  N49: LED7.cathode, R19.Pin_0
  N50: LED8.cathode, R20.Pin_0
  N51: LED9.cathode, R21.Pin_0
  N52: LED10.cathode, R22.Pin_0
  N53: LED11.cathode, R23.Pin_0
  N54: LED12.cathode, R24.Pin_0
  N55: LED13.cathode, R25.Pin_0
  N56: U2.MAIN, J3.pin2
  N57: U2.NC, J3.pin1
  N58: U3.MAIN, J2.pin1
  N59: U3.NO, J2.pin2
  N60: U4.MAIN, J1.pin1
  N61: U4.NO, J1.pin2
